# Fritzing sketch Inferno (saved by Fritzing 0.9.3b)
circuit board: 8.46667cm x 5.64444cm
breadboards: 1

parts:
  ADC1 = MCP3008 [package=dil16]
  Raspberry_Pi_1 = Raspberry Pi 3 [part_number=RPI-3-V1.2]
  R3 = Resistor [tolerance=±5% resistance=1k package="2512 [SMD]"]
  R4 = Resistor [tolerance=±5% resistance=1k package="2512 [SMD]"]
  RTD_Probe_1_(Grill) = mystery part, 2 pins [chip_label=?]
  U1 = 2-Channel 5v Relay Shield [package=relay-2ch5v10a]
  U2 = 2-Channel 5v Relay Shield [package=relay-2ch5v10a]
  RTD_Probe_2_(probe) = mystery part, 2 pins [chip_label=?]
  LCD1 = LCD screen  # not connected
  20x4_LCD_Screen_w/_I2C_interface = mystery part, 4 pins [chip_label=?]
  Blower_circuit_(110V) = mystery part, 2 pins [chip_label=?]
  Igniter_circuit_(110V) = mystery part, 2 pins [chip_label=?]
  Auger_circuit_(110V) = mystery part, 2 pins [chip_label=?]

nets:
  N1: ADC1.CH0, R4.Pin_1, RTD_Probe_1_(Grill).pin2
  N2: ADC1.CH1, R3.Pin_1, RTD_Probe_2_(probe).pin2
  GND: ADC1.DGND, ADC1.AGND, Raspberry_Pi_1.GND, R3.Pin_0, R4.Pin_0, U1.GND, U2.GND, 20x4_LCD_Screen_w/_I2C_interface.pin4
  N3: ADC1.CS/SHDN, Raspberry_Pi_1.GIPO8
  N4: ADC1.Din, Raspberry_Pi_1.GIPO10
  N5: ADC1.Dout, Raspberry_Pi_1.GIPO9
  N6: ADC1.CLK, Raspberry_Pi_1.GIPO11
  VDD: ADC1.VREF, ADC1.VDD, Raspberry_Pi_1.3v3, RTD_Probe_1_(Grill).pin1, RTD_Probe_2_(probe).pin1, 20x4_LCD_Screen_w/_I2C_interface.pin3
  N7: Raspberry_Pi_1.GPIO2, 20x4_LCD_Screen_w/_I2C_interface.pin2
  N8: Raspberry_Pi_1.GPIO3, 20x4_LCD_Screen_w/_I2C_interface.pin1
  N9: Raspberry_Pi_1.GIPO22, U2.IN1
  N10: Raspberry_Pi_1.GIPO21, U1.IN1
  N11: Raspberry_Pi_1.GIPO23, U2.IN2
  VCC: Raspberry_Pi_1.5V, U1.VCC, U2.VCC
  N12: U1.K1-Off, Blower_circuit_(110V).pin1
  N13: U1.K1-On, Blower_circuit_(110V).pin2
  N14: U2.K1-Off, Auger_circuit_(110V).pin1
  N15: U2.K1-On, Auger_circuit_(110V).pin2
  N16: U2.K2-Off, Igniter_circuit_(110V).pin1
  N17: U2.K2-On, Igniter_circuit_(110V).pin2

custom parts:
  2-Channel 5v Relay Shield: 2 Channel 5v Relay Shield w. 2x SPD-06VDC-SD-C
